# Fritzing sketch test1 (saved by Fritzing 0.9.3b)
circuit board: 9cm x 15cm
breadboards: 1

parts:
  S13 = Pushbutton [package="[THT]"]
  S14 = Pushbutton [package="[THT]"]
  S15 = Pushbutton [package="[THT]"]
  S16 = Pushbutton [package="[THT]"]
  S17 = Pushbutton [package="[THT]"]
  C2 = Capacitor Polarized [package=panasonic_c]
  SW5 = DIP Switch 8 Position [package=dipswitch-08]
  D126 = Rectifier Diode [part_number=1N4001 package="300 mil [THT]"]
  D127 = Rectifier Diode [part_number=1N4001 package="300 mil [THT]"]
  5V = double row female pin header, 2 pins [form="♀ (female)"]
  1 = female pin header, 16 pins [form="♀ (female)"]
  32 = female pin header, 16 pins [form="♀ (female)"]
  3_3V = double row female pin header, 2 pins [form="♀ (female)"]
  sensorIR1 = female pin header, 3 pins [form="♀ (female)"]
  Trắng-Xanh1 = double row female pin header, 2 pins [form="♀ (female)"]
  sensorIR2 = female pin header, 3 pins [form="♀ (female)"]
  Trắng-Xanh2 = double row female pin header, 2 pins [form="♀ (female)"]
  V1 = female pin header, 3 pins [form="♀ (female)"]
  V2 = female pin header, 3 pins [form="♀ (female)"]
  I2 = female pin header, 3 pins [form="♀ (female)"]
  I1 = female pin header, 3 pins [form="♀ (female)"]
  sensorIR3 = female pin header, 3 pins [form="♀ (female)"]
  sensorIR4 = female pin header, 3 pins [form="♀ (female)"]
  -Thu1 = double row female pin header, 2 pins [form="♀ (female)"]
  -Thu2 = double row female pin header, 2 pins [form="♀ (female)"]
  16 = female pin header, 8 pins [form="♀ (female)"]
  1_2 = female pin header, 8 pins [form="♀ (female)"]
  D132 = Rectifier Diode [part_number=1N4001 package="300 mil [THT]"]
  D133 = Rectifier Diode [part_number=1N4001 package="300 mil [THT]"]
  D134 = Rectifier Diode [part_number=1N4001 package="300 mil [THT]"]
  D135 = Rectifier Diode [part_number=1N4001 package="300 mil [THT]"]
  D136 = Rectifier Diode [part_number=1N4001 package="300 mil [THT]"]
  D137 = Rectifier Diode [part_number=1N4001 package="300 mil [THT]"]
  VAR_3 = female pin header, 3 pins [form="♀ (female)"]
  VAR_2 = female pin header, 3 pins [form="♀ (female)"]
  VAR_1 = female pin header, 3 pins [form="♀ (female)"]
  J1 = female pin header, 3 pins [form="♀ (female)"]
  J2 = female pin header, 3 pins [form="♀ (female)"]
  +2 = female pin header, 3 pins [form="♀ (female)"]
  +1 = female pin header, 3 pins [form="♀ (female)"]
  Nokia_5110_LCD_Module2 = Nokia 5110 LCD basado en PCD8544
  Linh_kiện6 = Arduino Mega 2560 (Rev3)

nets:
  N1: S13.Pin_1, S13.Pin_2, Linh_kiện6.RESET
  GND: S13.Pin_3, S13.Pin_4, S14.Pin_3, S14.Pin_4, S15.Pin_3, S15.Pin_4, S16.Pin_3, S16.Pin_4, S17.Pin_3, S17.Pin_4, C2.-, 5V.pin1, 32.pin12, 32.pin15, 3_3V.pin2, sensorIR1.pin2, sensorIR2.pin2, V1.pin3, V2.pin3, I2.pin3, I1.pin3, D134.cathode, D135.cathode, VAR_3.pin1, VAR_2.pin1, VAR_1.pin1, Nokia_5110_LCD_Module2.GND, Linh_kiện6.GND
  N2: S14.Pin_1, S14.Pin_2, Linh_kiện6.D21/SCL, Linh_kiện6.SCL
  N3: S15.Pin_1, S15.Pin_2, Linh_kiện6.D20/SDA, Linh_kiện6.SDA
  N4: S16.Pin_1, S16.Pin_2, Linh_kiện6.D0_RX0
  N5: S17.Pin_1, S17.Pin_2, Linh_kiện6.D1_TX0
  VCC: C2.+, Nokia_5110_LCD_Module2.VCC, Nokia_5110_LCD_Module2.LIGHT, Linh_kiện6.5V
  N6: SW5.1, 3_3V.pin1
  N7: SW5.2, SW5.3, 5V.pin2, V1.pin2, V2.pin2
  N8: SW5.14, 1.pin10, 32.pin1
  N9: SW5.15, -Thu1.pin1, -Thu2.pin1, 16.pin3, 16.pin6, 16.pin8, VAR_3.pin3
  N10: SW5.16, D126.anode, D127.anode, 1.pin11, 1.pin14, sensorIR1.pin3, sensorIR2.pin3, VAR_2.pin3, VAR_1.pin3, +2.pin1, +1.pin1
  N11: D126.cathode, 32.pin11, VAR_2.pin2, +1.pin2, +1.pin3
  N12: D127.cathode, 32.pin14, VAR_1.pin2, +2.pin2, +2.pin3
  N13: 1.pin1, 1.pin6
  N14: 1.pin2, 1.pin3
  N15: 1.pin5, D132.anode
  N16: 1.pin7, 1.pin8
  N17: 1.pin12, Linh_kiện6.D24
  N18: 1.pin13, Trắng-Xanh2.pin1
  N19: 1.pin15, Linh_kiện6.D25
  N20: 1.pin16, Trắng-Xanh1.pin1
  N21: 32.pin3, 32.pin4
  N22: 32.pin5, 32.pin10
  N23: 32.pin6, D137.anode
  N24: 32.pin8, 32.pin9
  N25: 32.pin13, Trắng-Xanh2.pin2
  N26: 32.pin16, Trắng-Xanh1.pin2
  N27: sensorIR1.pin1, Linh_kiện6.D22
  N28: sensorIR2.pin1, Linh_kiện6.D23
  N29: V1.pin1, Linh_kiện6.A0
  N30: V2.pin1, Linh_kiện6.A1
  N31: I2.pin1, D136.cathode, D137.cathode
  N32: I2.pin2, Linh_kiện6.A2
  N33: I1.pin1, D132.cathode, D133.cathode
  N34: I1.pin2, Linh_kiện6.A3
  N35: sensorIR3.pin1, Linh_kiện6.D26
  N36: sensorIR3.pin2, D135.anode
  N37: sensorIR3.pin3, sensorIR4.pin3, Linh_kiện6.3V3
  N38: sensorIR4.pin1, Linh_kiện6.D27
  N39: sensorIR4.pin2, D134.anode
  N40: -Thu1.pin2, 16.pin4
  N41: -Thu2.pin2, 16.pin5
  N42: 16.pin1, D136.anode
  N43: 16.pin2, 16.pin7, VAR_3.pin2
  N44: 1_2.pin2, 1_2.pin3
  N45: 1_2.pin4, D133.anode
  N46: 1_2.pin7, 1_2.pin8
  N47: J1.pin1, J1.pin2, J1.pin3
  N48: J2.pin1, J2.pin2, J2.pin3
  N49: Nokia_5110_LCD_Module2.RST, Linh_kiện6.D6_PWM
  N50: Nokia_5110_LCD_Module2.CE, Linh_kiện6.D7_PWM
  N51: Nokia_5110_LCD_Module2.DC, Linh_kiện6.D5_PWM
  N52: Nokia_5110_LCD_Module2.DIN, Linh_kiện6.D4_PWM
  N53: Nokia_5110_LCD_Module2.CLK, Linh_kiện6.D3_PWM

notes:
  Chú thích: Board có 2 nửa không nối với nhau: Đỏ +5V; Cam +3.3V; Đen: GND; Trắng: Out

custom parts:
  Nokia 5110 LCD basado en PCD8544: Módulo Nokia 5110 LCD basado en el controlador PCD8544. Versión de 8 pines (sólo entrada).
