# Fritzing sketch test2 (saved by Fritzing 0.9.3b)
circuit board: 5.84439cm x 10.6839cm
breadboards: 1

parts:
  Linh_kiện6 = Arduino Mega 2560 (Rev3)
  S13 = Pushbutton [package="[THT]"]
  S14 = Pushbutton [package="[THT]"]
  S15 = Pushbutton [package="[THT]"]
  S16 = Pushbutton [package="[THT]"]
  S17 = Pushbutton [package="[THT]"]
  SW5 = DIP Switch 8 Position [package=dipswitch-08]
  U15 = LM393 [package=so08]
  1 = female pin header, 16 pins [form="♀ (female)"]
  32 = female pin header, 16 pins [form="♀ (female)"]
  U16 = LM393 [package=so08]
  D127 = Rectifier Diode [part_number=1N4001 package="300 mil [THT]"]
  D126 = Rectifier Diode [part_number=1N4001 package="300 mil [THT]"]
  16 = female pin header, 8 pins [form="♀ (female)"]
  1_2 = female pin header, 8 pins [form="♀ (female)"]
  3_3V = female pin header, 1 pin [form="♀ (female)"]
  R78 = Resistor [tolerance=±5% resistance=10k package="0805 [SMD]"]
  R85 = Resistor [tolerance=±5% resistance=10k package="0805 [SMD]"]
  R79 = Resistor [tolerance=±5% resistance=10k package="0805 [SMD]"]
  R80 = Resistor [tolerance=±5% resistance=10k package="0805 [SMD]"]
  R83 = Resistor [tolerance=±5% resistance=10k package="0805 [SMD]"]
  R81 = Resistor [tolerance=±5% resistance=10k package="0805 [SMD]"]
  R84 = Resistor [tolerance=±5% resistance=10k package="0805 [SMD]"]
  R71 = Resistor [tolerance=±5% resistance=10k package="0805 [SMD]"]
  R70 = Resistor [tolerance=±5% resistance=10k package="0805 [SMD]"]
  R76 = Resistor [tolerance=±5% resistance=10k package="0805 [SMD]"]
  R75 = Resistor [tolerance=±5% resistance=10k package="0805 [SMD]"]
  R74 = Resistor [tolerance=±5% resistance=10k package="0805 [SMD]"]
  R77 = Resistor [tolerance=±5% resistance=10k package="0805 [SMD]"]
  R73 = Resistor [tolerance=±5% resistance=10k package="0805 [SMD]"]
  R72 = Resistor [tolerance=±5% resistance=10k package="0805 [SMD]"]
  R86 = Resistor [tolerance=±5% resistance=30k package="0805 [SMD]"]
  R88 = Resistor [tolerance=±5% resistance=7.5k package="0805 [SMD]"]
  R87 = Resistor [tolerance=±5% resistance=30k package="0805 [SMD]"]
  R89 = Resistor [tolerance=±5% resistance=7.5k package="0805 [SMD]"]
  R82 = Resistor [tolerance=±5% resistance=10k package="0805 [SMD]"]
  C26 = Tantalum Capacitor [capacitance=1µF package="A 3216 [SMD, tantalum]"]
  C27 = Tantalum Capacitor [capacitance=1µF package="A 3216 [SMD, tantalum]"]
  C24 = Tantalum Capacitor [capacitance=1µF package="A 3216 [SMD, tantalum]"]
  C25 = Tantalum Capacitor [capacitance=1µF package="A 3216 [SMD, tantalum]"]
  Nokia_5110_LCD_Module2 = Nokia 5110 LCD basado en PCD8544

nets:
  N1: Linh_kiện6.A0, R87.Pin_1, R89.Pin_1
  N2: Linh_kiện6.A1, R86.Pin_1, R88.Pin_1
  N3: Linh_kiện6.A2, 1.pin12
  N4: Linh_kiện6.A3, 32.pin11
  N5: Linh_kiện6.A4, 1_2.pin5
  N6: Linh_kiện6.A5, 16.pin8
  N7: Linh_kiện6.D21/SCL, S14.Pin_1, S14.Pin_2
  N8: Linh_kiện6.D20/SDA, S15.Pin_1, S15.Pin_2
  GND: Linh_kiện6.GND, S13.Pin_3, S13.Pin_4, S14.Pin_3, S14.Pin_4, S15.Pin_3, S15.Pin_4, S16.Pin_3, S16.Pin_4, S17.Pin_3, S17.Pin_4, U15.G1_V-, 1.pin1, 1.pin4, 32.pin2, 32.pin5, U16.G1_V-, 16.pin4, 16.pin5, R80.Pin_0, R71.Pin_1, R74.Pin_0, R82.Pin_1, C26.-, C27.-, C24.-, C25.-, Nokia_5110_LCD_Module2.GND
  N9: Linh_kiện6.RESET, S13.Pin_1, S13.Pin_2
  N10: Linh_kiện6.3V3, Nokia_5110_LCD_Module2.LIGHT
  N11: Linh_kiện6.D0_RX0, S16.Pin_1, S16.Pin_2
  N12: Linh_kiện6.D1_TX0, S17.Pin_1, S17.Pin_2
  N13: Linh_kiện6.D3_PWM, Nokia_5110_LCD_Module2.CLK
  N14: Linh_kiện6.D4_PWM, Nokia_5110_LCD_Module2.DIN
  N15: Linh_kiện6.D5_PWM, Nokia_5110_LCD_Module2.DC
  N16: Linh_kiện6.D6_PWM, Nokia_5110_LCD_Module2.RST
  N17: Linh_kiện6.D7_PWM, Nokia_5110_LCD_Module2.CE
  5V: Linh_kiện6.5V, Nokia_5110_LCD_Module2.VCC
  N18: Linh_kiện6.D22, U15.G1_OUT, R76.Pin_1
  N19: Linh_kiện6.D23, U15.G2_OUT, R73.Pin_0
  N20: Linh_kiện6.D24, 1.pin5
  N21: Linh_kiện6.D25, 1.pin2
  N22: Linh_kiện6.D26, U16.G2_OUT, R81.Pin_0
  N23: Linh_kiện6.D27, U16.G1_OUT, R85.Pin_1
  N24: SW5.1, SW5.2, SW5.3, 3_3V.pin1
  N25: SW5.14, 1.pin7, 32.pin16
  N26: SW5.15, 16.pin1, 16.pin3, 16.pin6, R78.Pin_1, R85.Pin_0, R79.Pin_0, R83.Pin_0, R81.Pin_1, R84.Pin_1
  N27: SW5.16, 1.pin3, 1.pin6, D127.anode, D126.anode, R70.Pin_1, R76.Pin_0, R75.Pin_0, R77.Pin_0, R73.Pin_1, R72.Pin_1, R86.Pin_0, R87.Pin_0
  N28: U15.G1_-IN, 32.pin3, D126.cathode, R71.Pin_0, R70.Pin_0, R89.Pin_0
  N29: U15.G1_+IN, 32.pin4, R75.Pin_1, C25.+
  N30: U15.G2_+IN, 32.pin1, R72.Pin_0, C24.+
  N31: U15.G2_-IN, 32.pin6, D127.cathode, R74.Pin_1, R77.Pin_1, R88.Pin_0
  N32: 1.pin9, 1.pin10
  N33: 1.pin11, 1.pin16
  N34: 1.pin14, 1.pin15
  N35: 32.pin7, 32.pin12
  N36: 32.pin8, 32.pin9
  N37: 32.pin13, 32.pin14
  N38: U16.G1_-IN, R78.Pin_0, R82.Pin_0
  N39: U16.G1_+IN, R79.Pin_1, C27.+
  N40: U16.G2_+IN, R84.Pin_0, C26.+
  N41: U16.G2_-IN, R80.Pin_1, R83.Pin_1
  N42: 1_2.pin1, 1_2.pin2
  N43: 1_2.pin6, 1_2.pin7

notes:
  Chú thích: Board có 2 nửa không nối với nhau: Đỏ +5V; Cam 3.3V; Đen: GND; Trắng: Out

custom parts:
  Nokia 5110 LCD basado en PCD8544: Módulo Nokia 5110 LCD basado en el controlador PCD8544. Versión de 8 pines (sólo entrada).
