# Fritzing sketch test3 (saved by Fritzing 0.9.3b)
circuit board: 10cm x 15cm

parts:
  J3 = female pin header, 3 pins [form="♀ (female)"]
  J4 = female pin header, 3 pins [form="♀ (female)"]
  Linh_kiện7 = Arduino Mega 2560 (Rev3)
  S18 = Pushbutton [package="[THT]"]
  S19 = Pushbutton [package="[THT]"]
  S20 = Pushbutton [package="[THT]"]
  S21 = Pushbutton [package="[THT]"]
  S22 = Pushbutton [package="[THT]"]
  SW6 = DIP Switch 8 Position [package=dipswitch-08]
  Nokia_5110_LCD_Module3 = Nokia 5110 LCD basado en PCD8544
  D138 = Rectifier Diode [part_number=1N4001 package="300 mil [THT]"]
  D139 = Rectifier Diode [part_number=1N4001 package="300 mil [THT]"]
  D140 = Rectifier Diode [part_number=1N4001 package="300 mil [THT]"]
  D141 = Rectifier Diode [part_number=1N4001 package="300 mil [THT]"]
  D142 = Rectifier Diode [part_number=1N4001 package="300 mil [THT]"]
  D143 = Rectifier Diode [part_number=1N4001 package="300 mil [THT]"]
  D144 = Rectifier Diode [part_number=1N4001 package="300 mil [THT]"]
  D145 = Rectifier Diode [part_number=1N4001 package="300 mil [THT]"]
  3_3V1 = double row female pin header, 2 pins [form="♀ (female)"]
  5V1 = double row female pin header, 2 pins [form="♀ (female)"]
  1 = female pin header, 8 pins [form="♀ (female)"]
  16 = female pin header, 8 pins [form="♀ (female)"]
  32 = female pin header, 16 pins [form="♀ (female)"]
  1_2 = female pin header, 16 pins [form="♀ (female)"]
  sensorIR5 = female pin header, 3 pins [form="♀ (female)"]
  sensorIR6 = female pin header, 3 pins [form="♀ (female)"]
  sensorIR7 = female pin header, 3 pins [form="♀ (female)"]
  sensorIR8 = female pin header, 3 pins [form="♀ (female)"]
  -Thu3 = double row female pin header, 2 pins [form="♀ (female)"]
  -Thu4 = double row female pin header, 2 pins [form="♀ (female)"]
  Trắng-Xanh3 = double row female pin header, 2 pins [form="♀ (female)"]
  Trắng-Xanh4 = double row female pin header, 2 pins [form="♀ (female)"]
  VAR_4 = female pin header, 3 pins [form="♀ (female)"]
  VAR_5 = female pin header, 3 pins [form="♀ (female)"]
  VAR_6 = female pin header, 3 pins [form="♀ (female)"]
  I3 = female pin header, 3 pins [form="♀ (female)"]
  I4 = female pin header, 3 pins [form="♀ (female)"]
  +3 = female pin header, 3 pins [form="♀ (female)"]
  +4 = female pin header, 3 pins [form="♀ (female)"]
  V3 = female pin header, 3 pins [form="♀ (female)"]
  V4 = female pin header, 3 pins [form="♀ (female)"]
  C3 = Capacitor Polarized [package=panasonic_c]

nets:
  N1: J3.pin1, J3.pin2, J3.pin3
  N2: J4.pin1, J4.pin2, J4.pin3
  N3: Linh_kiện7.A0, V4.pin1
  N4: Linh_kiện7.A1, V3.pin1
  N5: Linh_kiện7.A2, I4.pin2
  N6: Linh_kiện7.A3, I3.pin2
  N7: Linh_kiện7.D21/SCL, Linh_kiện7.SCL, S19.Pin_1, S19.Pin_2
  N8: Linh_kiện7.D20/SDA, Linh_kiện7.SDA, S20.Pin_1, S20.Pin_2
  GND: Linh_kiện7.GND, S18.Pin_3, S18.Pin_4, S19.Pin_3, S19.Pin_4, S20.Pin_3, S20.Pin_4, S21.Pin_3, S21.Pin_4, S22.Pin_3, S22.Pin_4, Nokia_5110_LCD_Module3.GND, D140.cathode, D141.cathode, 3_3V1.pin2, 5V1.pin1, 32.pin12, 32.pin15, sensorIR7.pin2, sensorIR8.pin2, VAR_4.pin1, VAR_5.pin1, VAR_6.pin1, I3.pin3, I4.pin3, V3.pin3, V4.pin3, C3.-
  N9: Linh_kiện7.RESET, S18.Pin_1, S18.Pin_2
  N10: Linh_kiện7.3V3, sensorIR5.pin3, sensorIR6.pin3
  5V: Linh_kiện7.5V, Nokia_5110_LCD_Module3.VCC, Nokia_5110_LCD_Module3.LIGHT, C3.+
  N11: Linh_kiện7.D0_RX0, S21.Pin_1, S21.Pin_2
  N12: Linh_kiện7.D1_TX0, S22.Pin_1, S22.Pin_2
  N13: Linh_kiện7.D3_PWM, Nokia_5110_LCD_Module3.CLK
  N14: Linh_kiện7.D4_PWM, Nokia_5110_LCD_Module3.DIN
  N15: Linh_kiện7.D5_PWM, Nokia_5110_LCD_Module3.DC
  N16: Linh_kiện7.D6_PWM, Nokia_5110_LCD_Module3.RST
  N17: Linh_kiện7.D7_PWM, Nokia_5110_LCD_Module3.CE
  N18: Linh_kiện7.D22, sensorIR8.pin1
  N19: Linh_kiện7.D23, sensorIR7.pin1
  N20: Linh_kiện7.D24, 1_2.pin12
  N21: Linh_kiện7.D25, 1_2.pin15
  N22: Linh_kiện7.D26, sensorIR6.pin1
  N23: Linh_kiện7.D27, sensorIR5.pin1
  N24: SW6.1, 3_3V1.pin1
  N25: SW6.2, SW6.3, 5V1.pin2, V3.pin2, V4.pin2
  N26: SW6.14, 32.pin1, 1_2.pin10
  N27: SW6.15, 16.pin3, 16.pin6, 16.pin8, -Thu3.pin1, -Thu4.pin1, VAR_6.pin3
  N28: SW6.16, D144.anode, D145.anode, 1_2.pin11, 1_2.pin14, sensorIR7.pin3, sensorIR8.pin3, VAR_4.pin3, VAR_5.pin3, +3.pin1, +4.pin1
  N29: D138.cathode, D139.cathode, I4.pin1
  N30: D138.anode, 32.pin6
  N31: D139.anode, 16.pin1
  N32: D140.anode, sensorIR6.pin2
  N33: D141.anode, sensorIR5.pin2
  N34: D142.cathode, D143.cathode, I3.pin1
  N35: D142.anode, 1.pin4
  N36: D143.anode, 1_2.pin5
  N37: D144.cathode, 32.pin11, VAR_5.pin2, +4.pin2, +4.pin3
  N38: D145.cathode, 32.pin14, VAR_4.pin2, +3.pin2, +3.pin3
  N39: 1.pin2, 1.pin3
  N40: 1.pin7, 1.pin8
  N41: 16.pin2, 16.pin7, VAR_6.pin2
  N42: 16.pin4, -Thu4.pin2
  N43: 16.pin5, -Thu3.pin2
  N44: 32.pin3, 32.pin4
  N45: 32.pin5, 32.pin10
  N46: 32.pin8, 32.pin9
  N47: 32.pin13, Trắng-Xanh3.pin2
  N48: 32.pin16, Trắng-Xanh4.pin2
  N49: 1_2.pin1, 1_2.pin6
  N50: 1_2.pin2, 1_2.pin3
  N51: 1_2.pin7, 1_2.pin8
  N52: 1_2.pin13, Trắng-Xanh3.pin1
  N53: 1_2.pin16, Trắng-Xanh4.pin1

custom parts:
  Nokia 5110 LCD basado en PCD8544: Módulo Nokia 5110 LCD basado en el controlador PCD8544. Versión de 8 pines (sólo entrada).
